# Fritzing sketch wiring (saved by Fritzing 0.9.3b)

parts:
  M1 = >Wemos D1 R32
  J1 = SHT3X [form="♂ (male)" package=THT]  # not connected
  MH-Z19B = MH-Z19C
  J2 = BH1750 [form="♂ (male)" package=THT]  # not connected
  KY-1 = Keyes Relay [package=THT]
  D1 = Rectifier Diode [part_number=1N4001 package="300 mil [THT]"]
  Q1 = Basic FET P-Channel [package="TO220 [THT]"]
  T1 = LM35 Temperature Sensor [package="TO92 [THT]"]
  Q2 = Basic FET P-Channel [package="TO220 [THT]"]
  51_ohm = Resistor [tolerance=±5% resistance=220 package="1206 [SMD]"]
  ZS-042_RTC1 = ZS-042 RTC Module
  D2 = Rectifier Diode [part_number=1N4001 package="300 mil [THT]"]  # not connected
  D3 = Rectifier Diode [part_number=1N4001 package="300 mil [THT]"]
  51_ohm_2 = Resistor [tolerance=±5% resistance=220 package="1206 [SMD]"]
  lampu = 2.1mm Barrel Jack with Terminal Block
  Mist_maker = 2.1mm Barrel Jack with Terminal Block
  Power_supply = 2.1mm Barrel Jack with Terminal Block
  power_supply = 2.1mm Barrel Jack with Terminal Block
  power_supply_2 = 2.1mm Barrel Jack with Terminal Block
  solenoid = 2.1mm Barrel Jack with Terminal Block

nets:
  5V: M1.5V, MH-Z19B.Vin, KY-1.power, D3.cathode
  3V3: M1.3V3, ZS-042_RTC1.VCC
  GND: M1.GND, MH-Z19B.GND, D1.anode, T1.+Vs, ZS-042_RTC1.GND, power_supply_2.POS
  N1: M1.RX0, MH-Z19B.Rx
  N2: M1.TX0, MH-Z19B.Tx
  N3: M1.IO12, 51_ohm_2.Pin_1
  N4: M1.IO13, 51_ohm.Pin_1
  N5: M1.IO5, T1.Vout
  N6: M1.SDA, ZS-042_RTC1.SDA
  N7: M1.SCL, ZS-042_RTC1.SCL
  N8: KY-1.ground, T1.GND, D3.anode
  N9: KY-1.C, power_supply.POS
  N10: KY-1.NO, lampu.POS
  N11: Q1.source, Mist_maker.NEG
  N12: Q2.drain, Power_supply.NEG
  N13: Q2.source, solenoid.NEG
  N14: lampu.NEG, power_supply.NEG
  N15: Mist_maker.POS, power_supply_2.NEG
  N16: Power_supply.POS, solenoid.POS

custom parts:
  >Wemos D1 R32: Wemos D1 R32 - This board is used with dual-mode Wi-Fi and Bluetooth chips, which is safe, reliable, and scalable to a variety of applications. DC in 5V-12V, 1 analog input(3.2V max input), a Micro USB connection, Compatible with D1 R32=WiFi+bluetooth+UNO
  SHT3X: SHT31 SHT31-D Temperature & Humidity Sensor Breakout
  MH-Z19C: CO2-Sensor https://www.winsen-sensor.com/
  BH1750: BH1750FVI is an digital Ambient Light Sensor IC for I2 C bus interface. This IC is the most suitable to obtain the ambient light data for adjusting LCD and Keypad backlight power of Mobile phone. It is possible to detect wide range at High resolution.
  Keyes Relay: The Keyes 5V relay module is suitable for SCM development, home appliance control. It uses a 5V~12V TIL control signal which can control DC / AC signal.
